// Logisim project Decryptor.circ as structural Verilog: 11 circuits, main circuit AES Decryption
module AES_Decryption (
  input  clk,
  input  [7:0] x34,
  input  [7:0] x33,
  input  [7:0] x32,
  input  [7:0] x31,
  input  [7:0] x24,
  input  [7:0] x23,
  input  [7:0] x22,
  input  [7:0] x21,
  input  [7:0] x14,
  input  [7:0] x13,
  input  [7:0] x12,
  input  [7:0] x11,
  input  [7:0] x04,
  input  [7:0] x03,
  input  [7:0] x02,
  input  [7:0] x01,
  input  [31:0] k0_1,
  input  [31:0] k0_4,
  input  [31:0] k0_2,
  input  [31:0] k0_3,
  output Finished,
  output [7:0] y0_1,
  output [7:0] y0_2,
  output [7:0] y0_3,
  output [7:0] y0_4,
  output [7:0] y1_1,
  output [7:0] y1_2,
  output [7:0] y1_3,
  output [7:0] y1_4,
  output [7:0] y2_1,
  output [7:0] y2_2,
  output [7:0] y2_3,
  output [7:0] y2_4,
  output [7:0] y3_1,
  output [7:0] y3_2,
  output [7:0] y3_3,
  output [7:0] y3_4
);

  wire EncryptionControl, multiplexer_17_out, nand_1_out, not_1_out, not_2_out;
  wire [3:0] RoundControl__1, RoundControl__2;
  wire [7:0] addroundkey_1_s00_2, addroundkey_1_s01_2, addroundkey_1_s02_2, addroundkey_1_s03_2,
       addroundkey_1_s10_2, addroundkey_1_s11_2, addroundkey_1_s12_2, addroundkey_1_s13_2,
       addroundkey_1_s20_2, addroundkey_1_s21_2, addroundkey_1_s22_2, addroundkey_1_s23_2,
       addroundkey_1_s30_2, addroundkey_1_s31_2, addroundkey_1_s32_2, addroundkey_1_s33_2,
       mixcolumns_r_1_s00_2, mixcolumns_r_1_s01_2, mixcolumns_r_1_s02_2, mixcolumns_r_1_s03_2,
       mixcolumns_r_1_s10_2, mixcolumns_r_1_s11_2, mixcolumns_r_1_s12_2, mixcolumns_r_1_s13_2,
       mixcolumns_r_1_s20_2, mixcolumns_r_1_s21_2, mixcolumns_r_1_s22_2, mixcolumns_r_1_s23_2,
       mixcolumns_r_1_s30_2, mixcolumns_r_1_s31_2, mixcolumns_r_1_s32_2, mixcolumns_r_1_s33_2,
       multiplexer_1_out, multiplexer_2_out, multiplexer_3_out, multiplexer_4_out, multiplexer_5_out,
       multiplexer_6_out, multiplexer_7_out, multiplexer_8_out, multiplexer_9_out, multiplexer_10_out,
       multiplexer_11_out, multiplexer_12_out, multiplexer_13_out, multiplexer_14_out, multiplexer_15_out,
       multiplexer_16_out, s00, s01, s02, s03, s10, s11, s12, s13, s20, s21, s22, s23, s30, s31, s32, s33,
       shiftrows_r_1_s00_2, shiftrows_r_1_s01_2, shiftrows_r_1_s02_2, shiftrows_r_1_s03_2,
       shiftrows_r_1_s10_2, shiftrows_r_1_s11_2, shiftrows_r_1_s12_2, shiftrows_r_1_s13_2,
       shiftrows_r_1_s20_2, shiftrows_r_1_s21_2, shiftrows_r_1_s22_2, shiftrows_r_1_s23_2,
       shiftrows_r_1_s30_2, shiftrows_r_1_s31_2, shiftrows_r_1_s32_2, shiftrows_r_1_s33_2,
       subbytes_r_1_s00_2, subbytes_r_1_s01_2, subbytes_r_1_s02_2, subbytes_r_1_s03_2, subbytes_r_1_s10_2,
       subbytes_r_1_s11_2, subbytes_r_1_s12_2, subbytes_r_1_s13_2, subbytes_r_1_s20_2, subbytes_r_1_s21_2,
       subbytes_r_1_s22_2, subbytes_r_1_s23_2, subbytes_r_1_s30_2, subbytes_r_1_s31_2, subbytes_r_1_s32_2,
       subbytes_r_1_s33_2, w00, w01, w02, w03, w10, w11, w12, w13, w20, w21, w22, w23, w30, w31, w32, w33;
  wire [31:0] k0_1_t, k0_2_t, k0_3_t, k0_4_t, k1_1, k1_2, k1_3, k1_4, k2_1, k2_2, k2_3, k2_4, k3_1, k3_2,
       k3_3, k3_4, k4_1, k4_2, k4_3, k4_4, k5_1, k5_2, k5_3, k5_4, k6_1, k6_2, k6_3, k6_4, k7_1, k7_2, k7_3,
       k7_4, k8_1, k8_2, k8_3, k8_4, k9_1, k9_2, k9_3, k9_4, multiplexer_18_out, multiplexer_19_out,
       multiplexer_20_out, multiplexer_21_out;

  AddRoundKey addroundkey_1 (
    .s00(x01), .s01(x11), .s10(x02), .s11(x12), .s20(x03), .s21(x13), .s30(x04), .s31(x14), .s02(x21),
    .s03(x31), .s12(x22), .s13(x32), .s22(x23), .s23(x33), .s32(x24), .s33(x34), .S00_2(addroundkey_1_s00_2),
    .S01_2(addroundkey_1_s01_2), .S10_2(addroundkey_1_s10_2), .S11_2(addroundkey_1_s11_2),
    .S20_2(addroundkey_1_s20_2), .S21_2(addroundkey_1_s21_2), .S30_2(addroundkey_1_s30_2),
    .S31_2(addroundkey_1_s31_2), .S02_2(addroundkey_1_s02_2), .S03_2(addroundkey_1_s03_2),
    .S12_2(addroundkey_1_s12_2), .S13_2(addroundkey_1_s13_2), .S22_2(addroundkey_1_s22_2),
    .S23_2(addroundkey_1_s23_2), .S32_2(addroundkey_1_s32_2), .S33_2(addroundkey_1_s33_2), .Wi(k0_1_t),
    .Wi_2(k0_3_t), .Wi_1(k0_2_t), .Wi_3(k0_4_t));
  KeyGen keygen_1 (
    .clk(clk), .RoundControl(RoundControl__1), .k1_1(k9_1), .k2_1(k8_1), .k3_1(k7_1), .k4_1(k6_1),
    .k5_1(k5_1), .k6_1(k4_1), .k7_1(k3_1), .k8_1(k2_1), .k9_1(k1_1), .k10_1(k0_1_t), .k1_2(k9_2),
    .k2_2(k8_2), .k3_2(k7_2), .k4_2(k6_2), .k5_2(k5_2), .k6_2(k4_2), .k7_2(k3_2), .k8_2(k2_2), .k9_2(k1_2),
    .k10_2(k0_2_t), .k1_3(k9_3), .k2_3(k8_3), .k3_3(k7_3), .k4_3(k6_3), .k5_3(k5_3), .k6_3(k4_3),
    .k7_3(k3_3), .k8_3(k2_3), .k9_3(k1_3), .k10_3(k0_3_t), .k1_4(k9_4), .k2_4(k8_4), .k3_4(k7_4),
    .k4_4(k6_4), .k5_4(k5_4), .k6_4(k4_4), .k7_4(k3_4), .k8_4(k2_4), .k9_4(k1_4), .k10_4(k0_4_t),
    .k0_1(k0_1), .k0_2(k0_2), .k0_3(k0_3), .k0_4(k0_4));
  not not_1 (not_1_out, Finished);
  Multiplexer #(.width(8), .disabled(0), .enable("false")) multiplexer_1 (
    .in0(addroundkey_1_s33_2), .in1(w33), .out(multiplexer_1_out), .sel(EncryptionControl));
  Multiplexer #(.width(8), .disabled(0), .enable("false")) multiplexer_2 (
    .in0(addroundkey_1_s23_2), .in1(w23), .out(multiplexer_2_out), .sel(EncryptionControl));
  Multiplexer #(.width(8), .disabled(0), .enable("false")) multiplexer_3 (
    .in0(addroundkey_1_s13_2), .in1(w13), .out(multiplexer_3_out), .sel(EncryptionControl));
  Multiplexer #(.width(8), .disabled(0), .enable("false")) multiplexer_4 (
    .in0(addroundkey_1_s03_2), .in1(w03), .out(multiplexer_4_out), .sel(EncryptionControl));
  Multiplexer #(.width(8), .disabled(0), .enable("false")) multiplexer_5 (
    .in0(addroundkey_1_s32_2), .in1(w32), .out(multiplexer_5_out), .sel(EncryptionControl));
  Multiplexer #(.width(8), .disabled(0), .enable("false")) multiplexer_6 (
    .in0(addroundkey_1_s22_2), .in1(w22), .out(multiplexer_6_out), .sel(EncryptionControl));
  Multiplexer #(.width(8), .disabled(0), .enable("false")) multiplexer_7 (
    .in0(addroundkey_1_s12_2), .in1(w12), .out(multiplexer_7_out), .sel(EncryptionControl));
  Multiplexer #(.width(8), .disabled(0), .enable("false")) multiplexer_8 (
    .in0(addroundkey_1_s02_2), .in1(w02), .out(multiplexer_8_out), .sel(EncryptionControl));
  Multiplexer #(.width(8), .disabled(0), .enable("false")) multiplexer_9 (
    .in0(addroundkey_1_s31_2), .in1(w31), .out(multiplexer_9_out), .sel(EncryptionControl));
  Multiplexer #(.width(8), .disabled(0), .enable("false")) multiplexer_10 (
    .in0(addroundkey_1_s21_2), .in1(w21), .out(multiplexer_10_out), .sel(EncryptionControl));
  Multiplexer #(.width(8), .disabled(0), .enable("false")) multiplexer_11 (
    .in0(addroundkey_1_s11_2), .in1(w11), .out(multiplexer_11_out), .sel(EncryptionControl));
  Multiplexer #(.width(8), .disabled(0), .enable("false")) multiplexer_12 (
    .in0(addroundkey_1_s01_2), .in1(w01), .out(multiplexer_12_out), .sel(EncryptionControl));
  Multiplexer #(.width(8), .disabled(0), .enable("false")) multiplexer_13 (
    .in0(addroundkey_1_s30_2), .in1(w30), .out(multiplexer_13_out), .sel(EncryptionControl));
  Multiplexer #(.width(8), .disabled(0), .enable("false")) multiplexer_14 (
    .in0(addroundkey_1_s20_2), .in1(w20), .out(multiplexer_14_out), .sel(EncryptionControl));
  Multiplexer #(.width(8), .disabled(0), .enable("false")) multiplexer_15 (
    .in0(addroundkey_1_s10_2), .in1(w10), .out(multiplexer_15_out), .sel(EncryptionControl));
  Multiplexer #(.width(8), .disabled(0), .enable("false")) multiplexer_16 (
    .in0(addroundkey_1_s00_2), .in1(w00), .out(multiplexer_16_out), .sel(EncryptionControl));
  Register u_s33 (.D(multiplexer_1_out), .en(not_1_out), .Q(s33), .clk(clk));  // open: clr
  Register u_s23 (.D(multiplexer_2_out), .en(not_1_out), .Q(s23), .clk(clk));  // open: clr
  Register _13 (.D(multiplexer_3_out), .en(not_1_out), .Q(s13), .clk(clk));  // open: clr
  Register u_s03 (.D(multiplexer_4_out), .en(not_1_out), .Q(s03), .clk(clk));  // open: clr
  Register u_s32 (.D(multiplexer_5_out), .en(not_1_out), .Q(s32), .clk(clk));  // open: clr
  Register u_s22 (.D(multiplexer_6_out), .en(not_1_out), .Q(s22), .clk(clk));  // open: clr
  Register u_s12 (.D(multiplexer_7_out), .en(not_1_out), .Q(s12), .clk(clk));  // open: clr
  Register u_s02 (.D(multiplexer_8_out), .en(not_1_out), .Q(s02), .clk(clk));  // open: clr
  Register u_s31 (.D(multiplexer_9_out), .en(not_1_out), .Q(s31), .clk(clk));  // open: clr
  Register u_s21 (.D(multiplexer_10_out), .en(not_1_out), .Q(s21), .clk(clk));  // open: clr
  Register u_s11 (.D(multiplexer_11_out), .en(not_1_out), .Q(s11), .clk(clk));  // open: clr
  Register u_s01 (.D(multiplexer_12_out), .en(not_1_out), .Q(s01), .clk(clk));  // open: clr
  Register u_s30 (.D(multiplexer_13_out), .en(not_1_out), .Q(s30), .clk(clk));  // open: clr
  Register u_s20 (.D(multiplexer_14_out), .en(not_1_out), .Q(s20), .clk(clk));  // open: clr
  Register u_s10 (.D(multiplexer_15_out), .en(not_1_out), .Q(s10), .clk(clk));  // open: clr
  Register u_s00 (.D(multiplexer_16_out), .en(not_1_out), .Q(s00), .clk(clk));  // open: clr
  Counter #(.width(4), .max('hb), .ongoal("stay")) counter_1 (
    .Q(RoundControl__1), .carry(EncryptionControl), .clk(clk));  // open: load, D, count, clr
  not not_2 (not_2_out, EncryptionControl);
  Counter #(.width(4), .max('h9), .ongoal("stay")) counter_2 (
    .Q(RoundControl__2), .carry(Finished), .clk(clk), .clr(not_2_out));  // open: load, D, count
  LED led_1 (.in(Finished));
  MixColumns_r mixcolumns_r_1 (
    .s00(s00), .s01(s01), .s10(s10), .s11(s11), .s20(s20), .s21(s21), .s30(s30), .s31(s31), .s02(s02),
    .s03(s03), .s12(s12), .s13(s13), .s22(s22), .s23(s23), .s32(s32), .s33(s33),
    .S00_2(mixcolumns_r_1_s00_2), .S01_2(mixcolumns_r_1_s01_2), .S10_2(mixcolumns_r_1_s10_2),
    .S11_2(mixcolumns_r_1_s11_2), .S20_2(mixcolumns_r_1_s20_2), .S21_2(mixcolumns_r_1_s21_2),
    .S30_2(mixcolumns_r_1_s30_2), .S31_2(mixcolumns_r_1_s31_2), .S02_2(mixcolumns_r_1_s02_2),
    .S03_2(mixcolumns_r_1_s03_2), .S12_2(mixcolumns_r_1_s12_2), .S13_2(mixcolumns_r_1_s13_2),
    .S22_2(mixcolumns_r_1_s22_2), .S23_2(mixcolumns_r_1_s23_2), .S32_2(mixcolumns_r_1_s32_2),
    .S33_2(mixcolumns_r_1_s33_2), .Enable(multiplexer_17_out));
  ShiftRows____r shiftrows_r_1 (
    .s00(mixcolumns_r_1_s00_2), .s20(mixcolumns_r_1_s20_2), .s01(mixcolumns_r_1_s01_2),
    .s21(mixcolumns_r_1_s21_2), .s02(mixcolumns_r_1_s02_2), .s22(mixcolumns_r_1_s22_2),
    .s03(mixcolumns_r_1_s03_2), .s23(mixcolumns_r_1_s23_2), .s10(mixcolumns_r_1_s10_2),
    .s30(mixcolumns_r_1_s30_2), .s11(mixcolumns_r_1_s11_2), .s31(mixcolumns_r_1_s31_2),
    .s12(mixcolumns_r_1_s12_2), .s32(mixcolumns_r_1_s32_2), .s13(mixcolumns_r_1_s13_2),
    .s33(mixcolumns_r_1_s33_2), .S00_2(shiftrows_r_1_s00_2), .S20_2(shiftrows_r_1_s20_2),
    .S01_2(shiftrows_r_1_s01_2), .S21_2(shiftrows_r_1_s21_2), .S02_2(shiftrows_r_1_s02_2),
    .S22_2(shiftrows_r_1_s22_2), .S03_2(shiftrows_r_1_s03_2), .S23_2(shiftrows_r_1_s23_2),
    .S10_2(shiftrows_r_1_s10_2), .S30_2(shiftrows_r_1_s30_2), .S11_2(shiftrows_r_1_s11_2),
    .S31_2(shiftrows_r_1_s31_2), .S12_2(shiftrows_r_1_s12_2), .S32_2(shiftrows_r_1_s32_2),
    .S13_2(shiftrows_r_1_s13_2), .S33_2(shiftrows_r_1_s33_2));
  SubBytes_r subbytes_r_1 (
    .s00(shiftrows_r_1_s00_2), .s01(shiftrows_r_1_s01_2), .s10(shiftrows_r_1_s10_2),
    .s11(shiftrows_r_1_s11_2), .s20(shiftrows_r_1_s20_2), .s21(shiftrows_r_1_s21_2),
    .s30(shiftrows_r_1_s30_2), .s31(shiftrows_r_1_s31_2), .s02(shiftrows_r_1_s02_2),
    .s03(shiftrows_r_1_s03_2), .s12(shiftrows_r_1_s12_2), .s13(shiftrows_r_1_s13_2),
    .s22(shiftrows_r_1_s22_2), .s23(shiftrows_r_1_s23_2), .s32(shiftrows_r_1_s32_2),
    .s33(shiftrows_r_1_s33_2), .S00_2(subbytes_r_1_s00_2), .S01_2(subbytes_r_1_s01_2),
    .S10_2(subbytes_r_1_s10_2), .S11_2(subbytes_r_1_s11_2), .S20_2(subbytes_r_1_s20_2),
    .S21_2(subbytes_r_1_s21_2), .S30_2(subbytes_r_1_s30_2), .S31_2(subbytes_r_1_s31_2),
    .S02_2(subbytes_r_1_s02_2), .S03_2(subbytes_r_1_s03_2), .S12_2(subbytes_r_1_s12_2),
    .S13_2(subbytes_r_1_s13_2), .S22_2(subbytes_r_1_s22_2), .S23_2(subbytes_r_1_s23_2),
    .S32_2(subbytes_r_1_s32_2), .S33_2(subbytes_r_1_s33_2));
  AddRoundKey addroundkey_2 (
    .s00(subbytes_r_1_s00_2), .s01(subbytes_r_1_s01_2), .s10(subbytes_r_1_s10_2), .s11(subbytes_r_1_s11_2),
    .s20(subbytes_r_1_s20_2), .s21(subbytes_r_1_s21_2), .s30(subbytes_r_1_s30_2), .s31(subbytes_r_1_s31_2),
    .s02(subbytes_r_1_s02_2), .s03(subbytes_r_1_s03_2), .s12(subbytes_r_1_s12_2), .s13(subbytes_r_1_s13_2),
    .s22(subbytes_r_1_s22_2), .s23(subbytes_r_1_s23_2), .s32(subbytes_r_1_s32_2), .s33(subbytes_r_1_s33_2),
    .S00_2(w00), .S01_2(w01), .S10_2(w10), .S11_2(w11), .S20_2(w20), .S21_2(w21), .S30_2(w30), .S31_2(w31),
    .S02_2(w02), .S03_2(w03), .S12_2(w12), .S13_2(w13), .S22_2(w22), .S23_2(w23), .S32_2(w32), .S33_2(w33),
    .Wi(multiplexer_18_out), .Wi_2(multiplexer_20_out), .Wi_1(multiplexer_19_out), .Wi_3(multiplexer_21_out));
  // Probe on {s00, s10, s20, s30}
  // Probe on {s01, s11, s21, s31}
  // Probe on {s02, s12, s22, s32}
  // Probe on {s03, s13, s23, s33}
  Multiplexer #(.disabled(0), .enable("false")) multiplexer_17 (
    .in0(1'b0), .in1(1'b1), .out(multiplexer_17_out), .sel(nand_1_out));
  // Probe on {mixcolumns_r_1_s00_2, mixcolumns_r_1_s10_2, mixcolumns_r_1_s20_2, mixcolumns_r_1_s30_2}
  // Probe on {mixcolumns_r_1_s01_2, mixcolumns_r_1_s11_2, mixcolumns_r_1_s21_2, mixcolumns_r_1_s31_2}
  // Probe on {mixcolumns_r_1_s02_2, mixcolumns_r_1_s12_2, mixcolumns_r_1_s22_2, mixcolumns_r_1_s32_2}
  // Probe on {mixcolumns_r_1_s03_2, mixcolumns_r_1_s13_2, mixcolumns_r_1_s23_2, mixcolumns_r_1_s33_2}
  // Probe on {shiftrows_r_1_s00_2, shiftrows_r_1_s10_2, shiftrows_r_1_s20_2, shiftrows_r_1_s30_2}
  // Probe on {shiftrows_r_1_s01_2, shiftrows_r_1_s11_2, shiftrows_r_1_s21_2, shiftrows_r_1_s31_2}
  // Probe on {shiftrows_r_1_s02_2, shiftrows_r_1_s12_2, shiftrows_r_1_s22_2, shiftrows_r_1_s32_2}
  // Probe on {shiftrows_r_1_s03_2, shiftrows_r_1_s13_2, shiftrows_r_1_s23_2, shiftrows_r_1_s33_2}
  // Probe on {subbytes_r_1_s00_2, subbytes_r_1_s10_2, subbytes_r_1_s20_2, subbytes_r_1_s30_2}
  // Probe on {subbytes_r_1_s01_2, subbytes_r_1_s11_2, subbytes_r_1_s21_2, subbytes_r_1_s31_2}
  // Probe on {subbytes_r_1_s02_2, subbytes_r_1_s12_2, subbytes_r_1_s22_2, subbytes_r_1_s32_2}
  // Probe on {subbytes_r_1_s03_2, subbytes_r_1_s13_2, subbytes_r_1_s23_2, subbytes_r_1_s33_2}
  nand nand_1 (nand_1_out, ~RoundControl__2[0], ~RoundControl__2[1], ~RoundControl__2[2], ~RoundControl__2[3]);  // NAND_Gate
  // Probe on w00
  // Probe on w10
  // Probe on w20
  // Probe on w30
  // Probe on w01
  // Probe on w11
  // Probe on w21
  // Probe on w31
  // Probe on w02
  // Probe on w12
  // Probe on w22
  // Probe on w32
  // Probe on w03
  // Probe on w13
  // Probe on w23
  // Probe on w33
  Multiplexer #(.select(4), .width(32), .disabled(0), .enable("false")) multiplexer_18 (
    .in0(k1_1), .in1(k2_1), .in2(k3_1), .in3(k4_1), .in4(k5_1), .in5(k6_1), .in6(k7_1), .in7(k8_1),
    .in8(k9_1), .in9(k0_1), .out(multiplexer_18_out), .sel(RoundControl__2));  // open: in10, in11, in12, in13, in14, in15
  Multiplexer #(.select(4), .width(32), .disabled(0), .enable("false")) multiplexer_19 (
    .in0(k1_2), .in1(k2_2), .in2(k3_2), .in3(k4_2), .in4(k5_2), .in5(k6_2), .in6(k7_2), .in7(k8_2),
    .in8(k9_2), .in9(k0_2), .out(multiplexer_19_out), .sel(RoundControl__2));  // open: in10, in11, in12, in13, in14, in15
  Multiplexer #(.select(4), .width(32), .disabled(0), .enable("false")) multiplexer_20 (
    .in0(k1_3), .in1(k2_3), .in2(k3_3), .in3(k4_3), .in4(k5_3), .in5(k6_3), .in6(k7_3), .in7(k8_3),
    .in8(k9_3), .in9(k0_3), .out(multiplexer_20_out), .sel(RoundControl__2));  // open: in10, in11, in12, in13, in14, in15
  Multiplexer #(.select(4), .width(32), .disabled(0), .enable("false")) multiplexer_21 (
    .in0(k1_4), .in1(k2_4), .in2(k3_4), .in3(k4_4), .in4(k5_4), .in5(k6_4), .in6(k7_4), .in7(k8_4),
    .in8(k9_4), .in9(k0_4), .out(multiplexer_21_out), .sel(RoundControl__2));  // open: in10, in11, in12, in13, in14, in15
  assign y0_1 = Finished ? w00 : 8'bz;  // Controlled_Buffer controlled_buffer_1
  assign y0_2 = Finished ? w10 : 8'bz;  // Controlled_Buffer controlled_buffer_2
  assign y0_3 = Finished ? w20 : 8'bz;  // Controlled_Buffer controlled_buffer_3
  assign y0_4 = Finished ? w30 : 8'bz;  // Controlled_Buffer controlled_buffer_4
  assign y1_1 = Finished ? w01 : 8'bz;  // Controlled_Buffer controlled_buffer_5
  assign y1_2 = Finished ? w11 : 8'bz;  // Controlled_Buffer controlled_buffer_6
  assign y1_3 = Finished ? w21 : 8'bz;  // Controlled_Buffer controlled_buffer_7
  assign y1_4 = Finished ? w31 : 8'bz;  // Controlled_Buffer controlled_buffer_8
  assign y2_1 = Finished ? w02 : 8'bz;  // Controlled_Buffer controlled_buffer_9
  assign y2_2 = Finished ? w12 : 8'bz;  // Controlled_Buffer controlled_buffer_10
  assign y2_3 = Finished ? w22 : 8'bz;  // Controlled_Buffer controlled_buffer_11
  assign y2_4 = Finished ? w32 : 8'bz;  // Controlled_Buffer controlled_buffer_12
  assign y3_1 = Finished ? w03 : 8'bz;  // Controlled_Buffer controlled_buffer_13
  assign y3_2 = Finished ? w13 : 8'bz;  // Controlled_Buffer controlled_buffer_14
  assign y3_3 = Finished ? w23 : 8'bz;  // Controlled_Buffer controlled_buffer_15
  assign y3_4 = Finished ? w33 : 8'bz;  // Controlled_Buffer controlled_buffer_16

  // Other names for the same wires on the sheet: k10_1[31:0] = k0_1; k10_2[31:0] = k0_2; k10_3[31:0] = k0_3;
  //   k10_4[31:0] = k0_4; LastRoundControl = Finished

  // Notes on the sheet:
  //   Adavanced Encryption Standard
  //   Cypher
  //   AES
  //   (128bit)
  //   Key (32bit*4)
  //   PlainText
endmodule

module KeyGen (
  input  [31:0] k0_1,
  input  [31:0] k0_2,
  input  [31:0] k0_3,
  input  [31:0] k0_4,
  input  clk,
  input  [3:0] RoundControl,
  output [31:0] k1_1,
  output [31:0] k2_1,
  output [31:0] k3_1,
  output [31:0] k4_1,
  output [31:0] k5_1,
  output [31:0] k6_1,
  output [31:0] k7_1,
  output [31:0] k8_1,
  output [31:0] k9_1,
  output [31:0] k10_1,
  output [31:0] k1_2,
  output [31:0] k2_2,
  output [31:0] k3_2,
  output [31:0] k4_2,
  output [31:0] k5_2,
  output [31:0] k6_2,
  output [31:0] k7_2,
  output [31:0] k8_2,
  output [31:0] k9_2,
  output [31:0] k10_2,
  output [31:0] k1_3,
  output [31:0] k2_3,
  output [31:0] k3_3,
  output [31:0] k4_3,
  output [31:0] k5_3,
  output [31:0] k6_3,
  output [31:0] k7_3,
  output [31:0] k8_3,
  output [31:0] k9_3,
  output [31:0] k10_3,
  output [31:0] k1_4,
  output [31:0] k2_4,
  output [31:0] k3_4,
  output [31:0] k4_4,
  output [31:0] k5_4,
  output [31:0] k6_4,
  output [31:0] k7_4,
  output [31:0] k8_4,
  output [31:0] k9_4,
  output [31:0] k10_4
);

  wire demultiplexer_1_out0, demultiplexer_1_out1, demultiplexer_1_out2, demultiplexer_1_out3,
       demultiplexer_1_out4, demultiplexer_1_out5, demultiplexer_1_out6, demultiplexer_1_out7,
       demultiplexer_1_out8, demultiplexer_1_out9, demultiplexer_2_out0, demultiplexer_2_out1,
       demultiplexer_2_out2, demultiplexer_2_out3, demultiplexer_2_out4, demultiplexer_2_out5,
       demultiplexer_2_out6, demultiplexer_2_out7, demultiplexer_2_out8, demultiplexer_2_out9,
       demultiplexer_3_out0, demultiplexer_3_out1, demultiplexer_3_out2, demultiplexer_3_out3,
       demultiplexer_3_out4, demultiplexer_3_out5, demultiplexer_3_out6, demultiplexer_3_out7,
       demultiplexer_3_out8, demultiplexer_3_out9, demultiplexer_4_out0, demultiplexer_4_out1,
       demultiplexer_4_out2, demultiplexer_4_out3, demultiplexer_4_out4, demultiplexer_4_out5,
       demultiplexer_4_out6, demultiplexer_4_out7, demultiplexer_4_out8, demultiplexer_4_out9;
  wire [7:0] s_box_1_out_2, s_box_2_out_2, s_box_3_out_2, s_box_4_out_2;
  wire [31:0] next0, next1, next2, next3, prev0, prev1, prev2, prev3, Rcon;

  // Probe on prev3
  // Probe on prev2
  // Probe on prev1
  // Probe on prev0
  Demultiplexer #(.select(4), .disabled(0), .enable("false")) demultiplexer_1 (
    .out0(demultiplexer_1_out0), .out1(demultiplexer_1_out1), .out2(demultiplexer_1_out2),
    .out3(demultiplexer_1_out3), .out4(demultiplexer_1_out4), .out5(demultiplexer_1_out5),
    .out6(demultiplexer_1_out6), .out7(demultiplexer_1_out7), .out8(demultiplexer_1_out8),
    .out9(demultiplexer_1_out9), .in(1'b1), .sel(RoundControl));  // open: out10, out11, out12, out13, out14, out15
  // Probe on k1_1
  // Probe on k1_2
  // Probe on k1_3
  // Probe on k1_4
  S_Box s_box_1 (.in_1(prev3[23:16]), .out_2(s_box_1_out_2));
  S_Box s_box_2 (.in_1(prev3[15:8]), .out_2(s_box_2_out_2));
  S_Box s_box_3 (.in_1(prev3[7:0]), .out_2(s_box_3_out_2));
  S_Box s_box_4 (.in_1(prev3[31:24]), .out_2(s_box_4_out_2));
  Register #(.width(32)) R1 (.D(next0), .en(demultiplexer_1_out0), .Q(k1_1), .clk(clk));  // open: clr
  Register #(.width(32)) R2 (.D(next0), .en(demultiplexer_1_out1), .Q(k2_1), .clk(clk));  // open: clr
  Register #(.width(32)) R3 (.D(next0), .en(demultiplexer_1_out2), .Q(k3_1), .clk(clk));  // open: clr
  Register #(.width(32)) R4 (.D(next0), .en(demultiplexer_1_out3), .Q(k4_1), .clk(clk));  // open: clr
  Register #(.width(32)) R5 (.D(next0), .en(demultiplexer_1_out4), .Q(k5_1), .clk(clk));  // open: clr
  Register #(.width(32)) R6 (.D(next0), .en(demultiplexer_1_out5), .Q(k6_1), .clk(clk));  // open: clr
  Register #(.width(32)) R7 (.D(next0), .en(demultiplexer_1_out6), .Q(k7_1), .clk(clk));  // open: clr
  Register #(.width(32)) R8 (.D(next0), .en(demultiplexer_1_out7), .Q(k8_1), .clk(clk));  // open: clr
  Register #(.width(32)) R9 (.D(next0), .en(demultiplexer_1_out8), .Q(k9_1), .clk(clk));  // open: clr
  Register #(.width(32)) R10 (.D(next0), .en(demultiplexer_1_out9), .Q(k10_1), .clk(clk));  // open: clr
  // Probe on next0
  // Probe on next1
  // Probe on next2
  // Probe on next3
  // Probe on k2_1
  // Probe on k2_2
  // Probe on k2_3
  // Probe on k2_4
  assign next0 = prev0 ^ Rcon ^ {s_box_1_out_2, s_box_2_out_2, s_box_3_out_2, s_box_4_out_2};  // XOR_Gate xor_1, 32 bits wide
  Multiplexer #(.select(4), .width(32), .disabled(0), .enable("false")) multiplexer_1 (
    .in0(k0_1), .in1(k1_1), .in2(k2_1), .in3(k3_1), .in4(k4_1), .in5(k5_1), .in6(k6_1), .in7(k7_1),
    .in8(k8_1), .in9(k9_1), .out(prev0), .sel(RoundControl));  // open: in10, in11, in12, in13, in14, in15
  assign next1 = prev1 ^ next0;  // XOR_Gate xor_2, 32 bits wide
  // Probe on prev2
  // Probe on nothing
  assign next2 = prev2 ^ next1;  // XOR_Gate xor_3, 32 bits wide
  // Probe on k3_1
  // Probe on k3_2
  // Probe on k3_3
  // Probe on k3_4
  assign next3 = prev3 ^ next2;  // XOR_Gate xor_4, 32 bits wide
  Demultiplexer #(.select(4), .disabled(0), .enable("false")) demultiplexer_2 (
    .out0(demultiplexer_2_out0), .out1(demultiplexer_2_out1), .out2(demultiplexer_2_out2),
    .out3(demultiplexer_2_out3), .out4(demultiplexer_2_out4), .out5(demultiplexer_2_out5),
    .out6(demultiplexer_2_out6), .out7(demultiplexer_2_out7), .out8(demultiplexer_2_out8),
    .out9(demultiplexer_2_out9), .in(1'b1), .sel(RoundControl));  // open: out10, out11, out12, out13, out14, out15
  // Probe on k4_1
  // Probe on k4_2
  // Probe on k4_3
  // Probe on k4_4
  Register #(.width(32)) R1_2 (.D(next1), .en(demultiplexer_2_out0), .Q(k1_2), .clk(clk));  // open: clr
  Register #(.width(32)) R2_2 (.D(next1), .en(demultiplexer_2_out1), .Q(k2_2), .clk(clk));  // open: clr
  Register #(.width(32)) R3_2 (.D(next1), .en(demultiplexer_2_out2), .Q(k3_2), .clk(clk));  // open: clr
  Register #(.width(32)) R4_2 (.D(next1), .en(demultiplexer_2_out3), .Q(k4_2), .clk(clk));  // open: clr
  Register #(.width(32)) R5_2 (.D(next1), .en(demultiplexer_2_out4), .Q(k5_2), .clk(clk));  // open: clr
  Register #(.width(32)) R6_2 (.D(next1), .en(demultiplexer_2_out5), .Q(k6_2), .clk(clk));  // open: clr
  Register #(.width(32)) R7_2 (.D(next1), .en(demultiplexer_2_out6), .Q(k7_2), .clk(clk));  // open: clr
  Register #(.width(32)) R8_2 (.D(next1), .en(demultiplexer_2_out7), .Q(k8_2), .clk(clk));  // open: clr
  Register #(.width(32)) R9_2 (.D(next1), .en(demultiplexer_2_out8), .Q(k9_2), .clk(clk));  // open: clr
  Register #(.width(32)) R10_2 (.D(next1), .en(demultiplexer_2_out9), .Q(k10_2), .clk(clk));  // open: clr
  // Probe on k5_1
  // Probe on k5_2
  // Probe on k5_3
  // Probe on k5_4
  Multiplexer #(.select(4), .width(32), .disabled(0), .enable("false")) multiplexer_2 (
    .in0(k0_2), .in1(k1_2), .in2(k2_2), .in3(k3_2), .in4(k4_2), .in5(k5_2), .in6(k6_2), .in7(k7_2),
    .in8(k8_2), .in9(k9_2), .out(prev1), .sel(RoundControl));  // open: in10, in11, in12, in13, in14, in15
  Demultiplexer #(.select(4), .disabled(0), .enable("false")) demultiplexer_3 (
    .out0(demultiplexer_3_out0), .out1(demultiplexer_3_out1), .out2(demultiplexer_3_out2),
    .out3(demultiplexer_3_out3), .out4(demultiplexer_3_out4), .out5(demultiplexer_3_out5),
    .out6(demultiplexer_3_out6), .out7(demultiplexer_3_out7), .out8(demultiplexer_3_out8),
    .out9(demultiplexer_3_out9), .in(1'b1), .sel(RoundControl));  // open: out10, out11, out12, out13, out14, out15
  // Probe on k6_1
  // Probe on k6_2
  // Probe on k6_3
  // Probe on k6_4
  Register #(.width(32)) R1_3 (.D(next2), .en(demultiplexer_3_out0), .Q(k1_3), .clk(clk));  // open: clr
  Register #(.width(32)) R2_3 (.D(next2), .en(demultiplexer_3_out1), .Q(k2_3), .clk(clk));  // open: clr
  Register #(.width(32)) R3_3 (.D(next2), .en(demultiplexer_3_out2), .Q(k3_3), .clk(clk));  // open: clr
  Register #(.width(32)) R4_3 (.D(next2), .en(demultiplexer_3_out3), .Q(k4_3), .clk(clk));  // open: clr
  Register #(.width(32)) R5_3 (.D(next2), .en(demultiplexer_3_out4), .Q(k5_3), .clk(clk));  // open: clr
  Register #(.width(32)) R6_3 (.D(next2), .en(demultiplexer_3_out5), .Q(k6_3), .clk(clk));  // open: clr
  Register #(.width(32)) R7_3 (.D(next2), .en(demultiplexer_3_out6), .Q(k7_3), .clk(clk));  // open: clr
  Register #(.width(32)) R8_3 (.D(next2), .en(demultiplexer_3_out7), .Q(k8_3), .clk(clk));  // open: clr
  Register #(.width(32)) R9_3 (.D(next2), .en(demultiplexer_3_out8), .Q(k9_3), .clk(clk));  // open: clr
  Register #(.width(32)) R10_3 (.D(next2), .en(demultiplexer_3_out9), .Q(k10_3), .clk(clk));  // open: clr
  // Probe on k7_1
  // Probe on k7_2
  // Probe on k7_3
  // Probe on k7_4
  Multiplexer #(.select(4), .width(32), .disabled(0), .enable("false")) multiplexer_3 (
    .in0(k0_3), .in1(k1_3), .in2(k2_3), .in3(k3_3), .in4(k4_3), .in5(k5_3), .in6(k6_3), .in7(k7_3),
    .in8(k8_3), .in9(k9_3), .out(prev2), .sel(RoundControl));  // open: in10, in11, in12, in13, in14, in15
  // Probe on k8_1
  // Probe on k8_2
  // Probe on k8_3
  // Probe on k8_4
  Demultiplexer #(.select(4), .disabled(0), .enable("false")) demultiplexer_4 (
    .out0(demultiplexer_4_out0), .out1(demultiplexer_4_out1), .out2(demultiplexer_4_out2),
    .out3(demultiplexer_4_out3), .out4(demultiplexer_4_out4), .out5(demultiplexer_4_out5),
    .out6(demultiplexer_4_out6), .out7(demultiplexer_4_out7), .out8(demultiplexer_4_out8),
    .out9(demultiplexer_4_out9), .in(1'b1), .sel(RoundControl));  // open: out10, out11, out12, out13, out14, out15
  // Probe on k9_1
  // Probe on k9_2
  // Probe on k9_3
  // Probe on k9_4
  Register #(.width(32)) R1_4 (.D(next3), .en(demultiplexer_4_out0), .Q(k1_4), .clk(clk));  // open: clr
  Register #(.width(32)) R2_4 (.D(next3), .en(demultiplexer_4_out1), .Q(k2_4), .clk(clk));  // open: clr
  Register #(.width(32)) R3_4 (.D(next3), .en(demultiplexer_4_out2), .Q(k3_4), .clk(clk));  // open: clr
  Register #(.width(32)) R4_4 (.D(next3), .en(demultiplexer_4_out3), .Q(k4_4), .clk(clk));  // open: clr
  Register #(.width(32)) R5_4 (.D(next3), .en(demultiplexer_4_out4), .Q(k5_4), .clk(clk));  // open: clr
  Register #(.width(32)) R6_4 (.D(next3), .en(demultiplexer_4_out5), .Q(k6_4), .clk(clk));  // open: clr
  Register #(.width(32)) R7_4 (.D(next3), .en(demultiplexer_4_out6), .Q(k7_4), .clk(clk));  // open: clr
  Register #(.width(32)) R8_4 (.D(next3), .en(demultiplexer_4_out7), .Q(k8_4), .clk(clk));  // open: clr
  Register #(.width(32)) R9_4 (.D(next3), .en(demultiplexer_4_out8), .Q(k9_4), .clk(clk));  // open: clr
  Register #(.width(32)) R10_4 (.D(next3), .en(demultiplexer_4_out9), .Q(k10_4), .clk(clk));  // open: clr
  // Probe on k10_1
  // Probe on k10_2
  // Probe on k10_3
  // Probe on k10_4
  Multiplexer #(.select(4), .width(32), .disabled(0), .enable("false")) multiplexer_4 (
    .in0(k0_4), .in1(k1_4), .in2(k2_4), .in3(k3_4), .in4(k4_4), .in5(k5_4), .in6(k6_4), .in7(k7_4),
    .in8(k8_4), .in9(k9_4), .out(prev3), .sel(RoundControl));  // open: in10, in11, in12, in13, in14, in15
  Multiplexer #(.select(4), .width(32), .disabled(0), .enable("false")) multiplexer_5 (
    .in0(32'h1000000), .in1(32'h2000000), .in2(32'h4000000), .in3(32'h8000000), .in4(32'h10000000),
    .in5(32'h20000000), .in6(32'h40000000), .in7(32'h80000000), .in8(32'h1b000000), .in9(32'h36000000),
    .out(Rcon), .sel(RoundControl));  // open: in10, in11, in12, in13, in14, in15

  // Notes on the sheet:
  //   Rcon
endmodule

module AddRoundKey (
  input  [31:0] Wi,
  input  [31:0] Wi_1,
  input  [7:0] s00,
  input  [7:0] s01,
  input  [7:0] s10,
  input  [7:0] s11,
  input  [7:0] s20,
  input  [7:0] s21,
  input  [7:0] s30,
  input  [7:0] s31,
  input  [31:0] Wi_2,
  input  [31:0] Wi_3,
  input  [7:0] s02,
  input  [7:0] s03,
  input  [7:0] s12,
  input  [7:0] s13,
  input  [7:0] s22,
  input  [7:0] s23,
  input  [7:0] s32,
  input  [7:0] s33,
  output [7:0] S00_2,
  output [7:0] S01_2,
  output [7:0] S10_2,
  output [7:0] S11_2,
  output [7:0] S20_2,
  output [7:0] S21_2,
  output [7:0] S30_2,
  output [7:0] S31_2,
  output [7:0] S02_2,
  output [7:0] S03_2,
  output [7:0] S12_2,
  output [7:0] S13_2,
  output [7:0] S22_2,
  output [7:0] S23_2,
  output [7:0] S32_2,
  output [7:0] S33_2
);

  // Probe on s02
  // Probe on s12
  // Probe on s22
  // Probe on s32
  assign S00_2 = Wi[31:24] ^ s00;  // XOR_Gate xor_1, 8 bits wide
  assign S10_2 = Wi[23:16] ^ s10;  // XOR_Gate xor_2, 8 bits wide
  assign S20_2 = Wi[15:8] ^ s20;  // XOR_Gate xor_3, 8 bits wide
  assign S30_2 = Wi[7:0] ^ s30;  // XOR_Gate xor_4, 8 bits wide
  assign S02_2 = Wi_2[31:24] ^ s02;  // XOR_Gate xor_5, 8 bits wide
  assign S12_2 = Wi_2[23:16] ^ s12;  // XOR_Gate xor_6, 8 bits wide
  assign S22_2 = Wi_2[15:8] ^ s22;  // XOR_Gate xor_7, 8 bits wide
  assign S32_2 = Wi_2[7:0] ^ s32;  // XOR_Gate xor_8, 8 bits wide
  // Probe on s03
  // Probe on s13
  // Probe on s23
  // Probe on s33
  assign S01_2 = Wi_1[31:24] ^ s01;  // XOR_Gate xor_9, 8 bits wide
  assign S11_2 = Wi_1[23:16] ^ s11;  // XOR_Gate xor_10, 8 bits wide
  assign S21_2 = Wi_1[15:8] ^ s21;  // XOR_Gate xor_11, 8 bits wide
  assign S31_2 = Wi_1[7:0] ^ s31;  // XOR_Gate xor_12, 8 bits wide
  assign S03_2 = Wi_3[31:24] ^ s03;  // XOR_Gate xor_13, 8 bits wide
  assign S13_2 = Wi_3[23:16] ^ s13;  // XOR_Gate xor_14, 8 bits wide
  assign S23_2 = Wi_3[15:8] ^ s23;  // XOR_Gate xor_15, 8 bits wide
  assign S33_2 = Wi_3[7:0] ^ s33;  // XOR_Gate xor_16, 8 bits wide
endmodule

module SubBytes_r (
  input  [7:0] s00,
  input  [7:0] s01,
  input  [7:0] s10,
  input  [7:0] s11,
  input  [7:0] s20,
  input  [7:0] s21,
  input  [7:0] s30,
  input  [7:0] s31,
  input  [7:0] s02,
  input  [7:0] s03,
  input  [7:0] s12,
  input  [7:0] s13,
  input  [7:0] s22,
  input  [7:0] s23,
  input  [7:0] s32,
  input  [7:0] s33,
  output [7:0] S00_2,
  output [7:0] S01_2,
  output [7:0] S10_2,
  output [7:0] S11_2,
  output [7:0] S20_2,
  output [7:0] S21_2,
  output [7:0] S30_2,
  output [7:0] S31_2,
  output [7:0] S02_2,
  output [7:0] S03_2,
  output [7:0] S12_2,
  output [7:0] S13_2,
  output [7:0] S22_2,
  output [7:0] S23_2,
  output [7:0] S32_2,
  output [7:0] S33_2
);

  S_Box_r s_box_r_1 (.in_1(s00), .out_2(S00_2));
  S_Box_r s_box_r_2 (.in_1(s10), .out_2(S10_2));
  S_Box_r s_box_r_3 (.in_1(s20), .out_2(S20_2));
  S_Box_r s_box_r_4 (.in_1(s30), .out_2(S30_2));
  S_Box_r s_box_r_5 (.in_1(s02), .out_2(S02_2));
  S_Box_r s_box_r_6 (.in_1(s12), .out_2(S12_2));
  S_Box_r s_box_r_7 (.in_1(s22), .out_2(S22_2));
  S_Box_r s_box_r_8 (.in_1(s32), .out_2(S32_2));
  S_Box_r s_box_r_9 (.in_1(s01), .out_2(S01_2));
  S_Box_r s_box_r_10 (.in_1(s11), .out_2(S11_2));
  S_Box_r s_box_r_11 (.in_1(s21), .out_2(S21_2));
  S_Box_r s_box_r_12 (.in_1(s31), .out_2(S31_2));
  S_Box_r s_box_r_13 (.in_1(s03), .out_2(S03_2));
  S_Box_r s_box_r_14 (.in_1(s13), .out_2(S13_2));
  S_Box_r s_box_r_15 (.in_1(s23), .out_2(S23_2));
  S_Box_r s_box_r_16 (.in_1(s33), .out_2(S33_2));
endmodule

module S_Box (
  input  [7:0] in_1,
  output [7:0] out_2
);

  ROM rom_1 (.addr(in_1), .data(out_2), .sel(1'b1));
  // Probe on out_2

  // Notes on the sheet:
  //   contents of rom_1 (hex, n*v repeats v):
  //   63 7c 77 7b f2 6b 6f c5 30 1 67 2b fe d7 ab 76 ca 82 c9 7d fa 59 47 f0 ad d4 a2 af 9c a4 72 c0 b7 fd
  //   93 26 36 3f f7 cc 34 a5 e5 f1 71 d8 31 15 4 c7 23 c3 18 96 5 9a 7 12 80 e2 eb 27 b2 75 9 83 2c 1a 1b
  //   6e 5a a0 52 3b d6 b3 29 e3 2f 84 53 d1 0 ed 20 fc b1 5b 6a cb be 39 4a 4c 58 cf d0 ef aa fb 43 4d 33
  //   85 45 f9 2 7f 50 3c 9f a8 51 a3 40 8f 92 9d 38 f5 bc b6 da 21 10 ff f3 d2 cd c 13 ec 5f 97 44 17 c4
  //   a7 7e 3d 64 5d 19 73 60 81 4f dc 22 2a 90 88 46 ee b8 14 de 5e b db e0 32 3a a 49 6 24 5c c2 d3 ac
  //   62 91 95 e4 79 e7 c8 37 6d 8d d5 4e a9 6c 56 f4 ea 65 7a ae 8 ba 78 25 2e 1c a6 b4 c6 e8 dd 74 1f 4b
  //   bd 8b 8a 70 3e b5 66 48 3 f6 e 61 35 57 b9 86 c1 1d 9e e1 f8 98 11 69 d9 8e 94 9b 1e 87 e9 ce 55 28
  //   df 8c a1 89 d bf e6 42 68 41 99 2d f b0 54 bb 16
endmodule

module S_Box_r (
  input  [7:0] in_1,
  output [7:0] out_2
);

  ROM rom_1 (.addr(in_1), .data(out_2), .sel(1'b1));
  // Probe on out_2

  // Notes on the sheet:
  //   contents of rom_1 (hex, n*v repeats v):
  //   52 9 6a d5 30 36 a5 38 bf 40 a3 9e 81 f3 d7 fb 7c e3 39 82 9b 2f ff 87 34 8e 43 44 c4 de e9 cb 54 7b
  //   94 32 a6 c2 23 3d ee 4c 95 b 42 fa c3 4e 8 2e a1 66 28 d9 24 b2 76 5b a2 49 6d 8b d1 25 72 f8 f6 64
  //   86 68 98 16 d4 a4 5c cc 5d 65 b6 92 6c 70 48 50 fd ed b9 da 5e 15 46 57 a7 8d 9d 84 90 d8 ab 0 8c bc
  //   d3 a f7 e4 58 5 b8 b3 45 6 d0 2c 1e 8f ca 3f f 2 c1 af bd 3 1 13 8a 6b 3a 91 11 41 4f 67 dc ea 97 f2
  //   cf ce f0 b4 e6 73 96 ac 74 22 e7 ad 35 85 e2 f9 37 e8 1c 75 df 6e 47 f1 1a 71 1d 29 c5 89 6f b7 62 e
  //   aa 18 be 1b fc 56 3e 4b c6 d2 79 20 9a db c0 fe 78 cd 5a f4 1f dd a8 33 88 7 c7 31 b1 12 10 59 27 80
  //   ec 5f 60 51 7f a9 19 b5 4a d 2d e5 7a 9f 93 c9 9c ef a0 e0 3b 4d ae 2a f5 b0 c8 eb bb 3c 83 53 99 61
  //   17 2b 4 7e ba 77 d6 26 e1 69 14 63 55 21 c 7d
endmodule

// ShiftRows
module ShiftRows____r (
  input  [7:0] s00,
  input  [7:0] s20,
  input  [7:0] s01,
  input  [7:0] s21,
  input  [7:0] s02,
  input  [7:0] s22,
  input  [7:0] s03,
  input  [7:0] s23,
  input  [7:0] s10,
  input  [7:0] s30,
  input  [7:0] s11,
  input  [7:0] s31,
  input  [7:0] s12,
  input  [7:0] s32,
  input  [7:0] s13,
  input  [7:0] s33,
  output [7:0] S00_2,
  output [7:0] S20_2,
  output [7:0] S01_2,
  output [7:0] S21_2,
  output [7:0] S02_2,
  output [7:0] S22_2,
  output [7:0] S03_2,
  output [7:0] S23_2,
  output [7:0] S10_2,
  output [7:0] S30_2,
  output [7:0] S11_2,
  output [7:0] S31_2,
  output [7:0] S12_2,
  output [7:0] S32_2,
  output [7:0] S13_2,
  output [7:0] S33_2
);

  // Probe on s00
  // Probe on s01
  // Probe on s02
  // Probe on s03

  assign S00_2 = s00;
  assign S01_2 = s01;
  assign S02_2 = s02;
  assign S03_2 = s03;
  assign S10_2 = s13;
  assign S11_2 = s10;
  assign S12_2 = s11;
  assign S13_2 = s12;
  assign S20_2 = s22;
  assign S21_2 = s23;
  assign S22_2 = s20;
  assign S23_2 = s21;
  assign S30_2 = s31;
  assign S31_2 = s32;
  assign S32_2 = s33;
  assign S33_2 = s30;
endmodule

// MixColumns
module MixColumns_r (
  input  Enable,
  input  [7:0] s00,
  input  [7:0] s01,
  input  [7:0] s10,
  input  [7:0] s11,
  input  [7:0] s20,
  input  [7:0] s21,
  input  [7:0] s30,
  input  [7:0] s31,
  input  [7:0] s02,
  input  [7:0] s03,
  input  [7:0] s12,
  input  [7:0] s13,
  input  [7:0] s22,
  input  [7:0] s23,
  input  [7:0] s32,
  input  [7:0] s33,
  output [7:0] S00_2,
  output [7:0] S01_2,
  output [7:0] S10_2,
  output [7:0] S11_2,
  output [7:0] S20_2,
  output [7:0] S21_2,
  output [7:0] S30_2,
  output [7:0] S31_2,
  output [7:0] S02_2,
  output [7:0] S03_2,
  output [7:0] S12_2,
  output [7:0] S13_2,
  output [7:0] S22_2,
  output [7:0] S23_2,
  output [7:0] S32_2,
  output [7:0] S33_2
);

  MixColumns_C__r mixcolumns_c_r_1 (
    .s0_c(s00), .s1_c(s10), .s2_c(s20), .s3_c(s30), .S0_c_2(S00_2), .S1_c_2(S10_2), .S2_c_2(S20_2),
    .S3_c_2(S30_2), .Enable(Enable));
  MixColumns_C__r mixcolumns_c_r_2 (
    .s0_c(s02), .s1_c(s12), .s2_c(s22), .s3_c(s32), .S0_c_2(S02_2), .S1_c_2(S12_2), .S2_c_2(S22_2),
    .S3_c_2(S32_2), .Enable(Enable));
  MixColumns_C__r mixcolumns_c_r_3 (
    .s0_c(s01), .s1_c(s11), .s2_c(s21), .s3_c(s31), .S0_c_2(S01_2), .S1_c_2(S11_2), .S2_c_2(S21_2),
    .S3_c_2(S31_2), .Enable(Enable));
  MixColumns_C__r mixcolumns_c_r_4 (
    .s0_c(s03), .s1_c(s13), .s2_c(s23), .s3_c(s33), .S0_c_2(S03_2), .S1_c_2(S13_2), .S2_c_2(S23_2),
    .S3_c_2(S33_2), .Enable(Enable));
endmodule

module MixColumns_C__r (
  input  [7:0] s0_c,
  input  [7:0] s1_c,
  input  [7:0] s2_c,
  input  [7:0] s3_c,
  input  Enable,
  output [7:0] S0_c_2,
  output [7:0] S1_c_2,
  output [7:0] S2_c_2,
  output [7:0] S3_c_2
);

  wire [7:0] demultiplexer_1_out0, demultiplexer_1_out1, demultiplexer_2_out0, demultiplexer_2_out1,
       demultiplexer_3_out0, demultiplexer_3_out1, demultiplexer_4_out0, demultiplexer_4_out1,
       matrixmul_r_1_out, matrixmul_r_2_out, matrixmul_r_3_out, matrixmul_r_4_out;

  Demultiplexer #(.width(8), .enable("false")) demultiplexer_1 (
    .out0(demultiplexer_1_out0), .out1(demultiplexer_1_out1), .in(s0_c), .sel(Enable));
  Demultiplexer #(.width(8), .enable("false")) demultiplexer_2 (
    .out0(demultiplexer_2_out0), .out1(demultiplexer_2_out1), .in(s1_c), .sel(Enable));
  Demultiplexer #(.width(8), .enable("false")) demultiplexer_3 (
    .out0(demultiplexer_3_out0), .out1(demultiplexer_3_out1), .in(s2_c), .sel(Enable));
  Demultiplexer #(.width(8), .enable("false")) demultiplexer_4 (
    .out0(demultiplexer_4_out0), .out1(demultiplexer_4_out1), .in(s3_c), .sel(Enable));
  MatrixMul_r matrixmul_r_1 (
    .out(matrixmul_r_1_out), .t0(demultiplexer_1_out1), .t1(demultiplexer_2_out1), .t2(demultiplexer_3_out1),
    .t3(demultiplexer_4_out1));
  MatrixMul_r matrixmul_r_2 (
    .out(matrixmul_r_2_out), .t0(demultiplexer_2_out1), .t1(demultiplexer_3_out1), .t2(demultiplexer_4_out1),
    .t3(demultiplexer_1_out1));
  MatrixMul_r matrixmul_r_3 (
    .out(matrixmul_r_3_out), .t0(demultiplexer_3_out1), .t1(demultiplexer_4_out1), .t2(demultiplexer_1_out1),
    .t3(demultiplexer_2_out1));
  MatrixMul_r matrixmul_r_4 (
    .out(matrixmul_r_4_out), .t0(demultiplexer_4_out1), .t1(demultiplexer_1_out1), .t2(demultiplexer_2_out1),
    .t3(demultiplexer_3_out1));
  Multiplexer #(.width(8), .enable("false")) multiplexer_1 (
    .in0(demultiplexer_1_out0), .in1(matrixmul_r_1_out), .out(S0_c_2), .sel(Enable));
  Multiplexer #(.width(8), .enable("false")) multiplexer_2 (
    .in0(demultiplexer_2_out0), .in1(matrixmul_r_2_out), .out(S1_c_2), .sel(Enable));
  Multiplexer #(.width(8), .enable("false")) multiplexer_3 (
    .in0(demultiplexer_3_out0), .in1(matrixmul_r_3_out), .out(S2_c_2), .sel(Enable));
  Multiplexer #(.width(8), .enable("false")) multiplexer_4 (
    .in0(demultiplexer_4_out0), .in1(matrixmul_r_4_out), .out(S3_c_2), .sel(Enable));
endmodule

module MatrixMul_r (
  input  [7:0] t0,
  input  [7:0] t1,
  input  [7:0] t2,
  input  [7:0] t3,
  output [7:0] out
);

  wire [7:0] fieldmul2_1_out_2, fieldmul2_2_out_2, fieldmul2_3_out_2, fieldmul2_4_out_2, fieldmul2_5_out_2,
       fieldmul2_6_out_2, fieldmul2_7_out_2, fieldmul2_8_out_2, fieldmul2_9_out_2, fieldmul2_10_out_2,
       fieldmul2_11_out_2, fieldmul2_12_out_2, xor_1_out, xor_2_out, xor_3_out, xor_4_out;

  // Probe on t0
  // Probe on t1
  // Probe on t2
  // Probe on t3
  FieldMul2 fieldmul2_1 (.in_1(fieldmul2_2_out_2), .out_2(fieldmul2_1_out_2));
  FieldMul2 fieldmul2_2 (.in_1(t0), .out_2(fieldmul2_2_out_2));
  FieldMul2 fieldmul2_3 (.in_1(fieldmul2_4_out_2), .out_2(fieldmul2_3_out_2));
  FieldMul2 fieldmul2_4 (.in_1(t1), .out_2(fieldmul2_4_out_2));
  FieldMul2 fieldmul2_5 (.in_1(fieldmul2_6_out_2), .out_2(fieldmul2_5_out_2));
  FieldMul2 fieldmul2_6 (.in_1(t2), .out_2(fieldmul2_6_out_2));
  FieldMul2 fieldmul2_7 (.in_1(t3), .out_2(fieldmul2_7_out_2));
  FieldMul2 fieldmul2_8 (.in_1(fieldmul2_7_out_2), .out_2(fieldmul2_8_out_2));
  FieldMul2 fieldmul2_9 (.in_1(fieldmul2_1_out_2), .out_2(fieldmul2_9_out_2));
  FieldMul2 fieldmul2_10 (.in_1(fieldmul2_3_out_2), .out_2(fieldmul2_10_out_2));
  FieldMul2 fieldmul2_11 (.in_1(fieldmul2_5_out_2), .out_2(fieldmul2_11_out_2));
  FieldMul2 fieldmul2_12 (.in_1(fieldmul2_8_out_2), .out_2(fieldmul2_12_out_2));
  // Probe on xor_1_out
  assign xor_1_out = fieldmul2_2_out_2 ^ fieldmul2_1_out_2 ^ fieldmul2_9_out_2;  // XOR_Gate xor_1, 8 bits wide
  // Probe on xor_2_out
  assign xor_2_out = t1 ^ fieldmul2_4_out_2 ^ fieldmul2_10_out_2;  // XOR_Gate xor_2, 8 bits wide
  assign xor_3_out = t2 ^ fieldmul2_5_out_2 ^ fieldmul2_11_out_2;  // XOR_Gate xor_3, 8 bits wide
  // Probe on xor_3_out
  assign xor_4_out = t3 ^ fieldmul2_12_out_2;  // XOR_Gate xor_4, 8 bits wide
  // Probe on xor_4_out
  assign out = xor_1_out ^ xor_2_out ^ xor_3_out ^ xor_4_out;  // XOR_Gate xor_5, 8 bits wide
endmodule

module FieldMul2 (
  input  [7:0] in_1,
  output [7:0] out_2
);

  wire [7:0] and_1_out, bit_extender_1_out, shifter_1_out;

  assign bit_extender_1_out = {{7{in_1[7]}}, in_1[7]};  // Bit_Extender bit_extender_1
  Shifter shifter_1 (.in(in_1), .\dist (3'b001), .out(shifter_1_out));
  assign and_1_out = 8'h1b & bit_extender_1_out;  // AND_Gate and_1, 8 bits wide
  assign out_2 = and_1_out ^ shifter_1_out;  // XOR_Gate xor_1, 8 bits wide
endmodule
