// Logisim project test.circ as structural Verilog: 1 circuit, main circuit main
module main (
  input  [31:0] in_1,
  input  [31:0] in_2,
  input  [31:0] in_3,
  input  [31:0] in_4,
  input  [31:0] in_5,
  input  [31:0] KEY,
  input  [31:0] in_7,
  input  [31:0] in_8
);

  wire aes_decryption_1_finished, aes_encryption_1_finished, clock_1_out, controlled_buffer_1_out,
       controlled_buffer_2_out, not_1_out;
  wire [7:0] aes_decryption_1_y0_1, aes_decryption_1_y0_2, aes_decryption_1_y0_3, aes_decryption_1_y0_4,
       aes_decryption_1_y1_1, aes_decryption_1_y1_2, aes_decryption_1_y1_3, aes_decryption_1_y1_4,
       aes_decryption_1_y2_1, aes_decryption_1_y2_2, aes_decryption_1_y2_3, aes_decryption_1_y2_4,
       aes_decryption_1_y3_1, aes_decryption_1_y3_2, aes_decryption_1_y3_3, aes_decryption_1_y3_4,
       aes_encryption_1_y1_1, aes_encryption_1_y1_2, aes_encryption_1_y1_3, aes_encryption_1_y1_4,
       aes_encryption_1_y2_1, aes_encryption_1_y2_2, aes_encryption_1_y2_3, aes_encryption_1_y2_4,
       aes_encryption_1_y3_1, aes_encryption_1_y3_2, aes_encryption_1_y3_3, aes_encryption_1_y3_4;
  wire [31:0] aes_encryption_1_y0_4;

  Clock clock_1 (.out(clock_1_out));
  assign controlled_buffer_1_out = not_1_out ? clock_1_out : 1'bz;  // Controlled_Buffer controlled_buffer_1
  not not_1 (not_1_out, aes_encryption_1_finished);
  AES_Encryption aes_encryption_1 (
    .x34(in_1[7:0]), .x33(in_1[15:8]), .x32(in_1[23:16]), .x31(in_1[31:24]), .x24(in_2[7:0]),
    .x23(in_2[15:8]), .x22(in_2[23:16]), .x21(in_2[31:24]), .x14(in_3[7:0]), .x13(in_3[15:8]),
    .x12(in_3[23:16]), .x11(in_3[31:24]), .x04(in_4[7:0]), .x03(in_4[15:8]), .x02(in_4[23:16]),
    .x01(in_4[31:24]), .clk(controlled_buffer_1_out), .k0_1(in_5), .k0_2(KEY), .k0_4(in_8), .k0_3(in_7),
    .y3_4(aes_encryption_1_y3_4), .y3_3(aes_encryption_1_y3_3), .y3_2(aes_encryption_1_y3_2),
    .y3_1(aes_encryption_1_y3_1), .y2_4(aes_encryption_1_y2_4), .y2_3(aes_encryption_1_y2_3),
    .y2_2(aes_encryption_1_y2_2), .y2_1(aes_encryption_1_y2_1), .y1_4(aes_encryption_1_y1_4),
    .y1_3(aes_encryption_1_y1_3), .y1_2(aes_encryption_1_y1_2), .y1_1(aes_encryption_1_y1_1),
    .y0_4(aes_encryption_1_y0_4[7:0]), .y0_3(aes_encryption_1_y0_4[15:8]),
    .y0_2(aes_encryption_1_y0_4[23:16]), .y0_1(aes_encryption_1_y0_4[31:24]),
    .Finished(aes_encryption_1_finished));
  // Probe on aes_encryption_1_y0_4
  // Probe on {aes_encryption_1_y1_1, aes_encryption_1_y1_2, aes_encryption_1_y1_3, aes_encryption_1_y1_4}
  // Probe on {aes_encryption_1_y2_1, aes_encryption_1_y2_2, aes_encryption_1_y2_3, aes_encryption_1_y2_4}
  // Probe on {aes_encryption_1_y3_1, aes_encryption_1_y3_2, aes_encryption_1_y3_3, aes_encryption_1_y3_4}
  assign controlled_buffer_2_out = aes_encryption_1_finished ? clock_1_out : 1'bz;  // Controlled_Buffer controlled_buffer_2
  AES_Decryption aes_decryption_1 (
    .clk(controlled_buffer_2_out), .y3_4(aes_decryption_1_y3_4), .y3_3(aes_decryption_1_y3_3),
    .y3_2(aes_decryption_1_y3_2), .y3_1(aes_decryption_1_y3_1), .y2_4(aes_decryption_1_y2_4),
    .y2_3(aes_decryption_1_y2_3), .y2_2(aes_decryption_1_y2_2), .y2_1(aes_decryption_1_y2_1),
    .y1_4(aes_decryption_1_y1_4), .y1_3(aes_decryption_1_y1_3), .y1_2(aes_decryption_1_y1_2),
    .y1_1(aes_decryption_1_y1_1), .y0_4(aes_decryption_1_y0_4), .y0_3(aes_decryption_1_y0_3),
    .y0_2(aes_decryption_1_y0_2), .y0_1(aes_decryption_1_y0_1), .x34(aes_encryption_1_y3_4),
    .x33(aes_encryption_1_y3_3), .x32(aes_encryption_1_y3_2), .x31(aes_encryption_1_y3_1),
    .x24(aes_encryption_1_y2_4), .x23(aes_encryption_1_y2_3), .x22(aes_encryption_1_y2_2),
    .x21(aes_encryption_1_y2_1), .x14(aes_encryption_1_y1_4), .x13(aes_encryption_1_y1_3),
    .x12(aes_encryption_1_y1_2), .x11(aes_encryption_1_y1_1), .x04(aes_encryption_1_y0_4[7:0]),
    .x03(aes_encryption_1_y0_4[15:8]), .x02(aes_encryption_1_y0_4[23:16]),
    .x01(aes_encryption_1_y0_4[31:24]), .k0_1(in_5), .k0_4(in_8), .k0_2(KEY), .k0_3(in_7),
    .Finished(aes_decryption_1_finished));
  LED led_1 (.in(aes_decryption_1_finished));
  // Probe on {aes_decryption_1_y3_1, aes_decryption_1_y3_2, aes_decryption_1_y3_3, aes_decryption_1_y3_4}
  // Probe on {aes_decryption_1_y2_1, aes_decryption_1_y2_2, aes_decryption_1_y2_3, aes_decryption_1_y2_4}
  // Probe on {aes_decryption_1_y1_1, aes_decryption_1_y1_2, aes_decryption_1_y1_3, aes_decryption_1_y1_4}
  // Probe on {aes_decryption_1_y0_1, aes_decryption_1_y0_2, aes_decryption_1_y0_3, aes_decryption_1_y0_4}

  // Notes on the sheet:
  //   Plain Text
  //   Cypher
  //   -1
  //   Plain text
endmodule
